# Fritzing sketch Circuit (saved by Fritzing 0.9.8b)

parts:
  MD1 = Maker Drive
  Mod1 = Raspberry Pi 4B
  M1 = DC Motor  # not connected
  M2 = DC Motor  # not connected
  BATT1 = 4xAA Switchable Battery Pack w/Bare Wire

nets:
  N1: MD1.VB+, BATT1.POS
  N2: MD1.VB-, BATT1.NEG
  N3: MD1.M1A_IO, Mod1.GPIO14
  N4: MD1.M1B_IO, Mod1.GPIO15
  GND: MD1.GND, Mod1.GND
  N5: MD1.M2A_IO, Mod1.GPIO18
  N6: MD1.M2B_IO, Mod1.GPIO23

custom parts:
  Maker Drive: Simplifying H-Bridge Motor Driver for Beginner.
  4xAA Switchable Battery Pack w/Bare Wire: 4xAA Switchable Battery Pack with Bare Wire connection
